// Logisim project 150120991_150120852.circ as structural Verilog
module fullAdder (
  input  a,
  input  b,
  input  cin,
  output s,
  output co
);

  wire and_1_out, and_2_out, and_3_out;

  ExactlyOne xor_1 (.out(s), .in0(a), .in1(b), .in2(cin));
  and and_1 (and_1_out, a, b);
  and and_2 (and_2_out, a, cin);
  and and_3 (and_3_out, b, cin);
  or or_1 (co, and_1_out, and_2_out, and_3_out);
endmodule

module _4bitAdder (
  input  [3:0] in_1,
  input  [3:0] in_2,
  input  Cin,
  output out_4,
  output out_5,
  output out_6,
  output out_7,
  output out_8
);

  wire fulladder_1_co, fulladder_2_co, fulladder_3_co;

  fullAdder fulladder_1 (.a(in_1[0]), .b(in_2[0]), .cin(Cin), .s(out_7), .co(fulladder_1_co));
  fullAdder fulladder_2 (.a(in_1[1]), .b(in_2[1]), .cin(fulladder_1_co), .s(out_6), .co(fulladder_2_co));
  fullAdder fulladder_3 (.a(in_1[2]), .b(in_2[2]), .cin(fulladder_2_co), .s(out_5), .co(fulladder_3_co));
  fullAdder fulladder_4 (.a(in_1[3]), .b(in_2[3]), .cin(fulladder_3_co), .s(out_4), .co(out_8));
endmodule

module _8bitAdder (
  input  [7:0] in_1,
  input  [7:0] in_2,
  input  Cin,
  output out_4,
  output out_5,
  output out_6,
  output out_7,
  output out_8,
  output out_9,
  output out_10,
  output out_11,
  output Cout
);

  wire n4bitadder_1_out_8;

  _4bitAdder u_4bitadder_1 (
    .in_1(in_1[3:0]), .in_2(in_2[3:0]), .Cin(Cin), .out_4(out_8), .out_5(out_9), .out_6(out_10),
    .out_7(out_11), .out_8(n4bitadder_1_out_8));
  _4bitAdder u_4bitadder_2 (
    .in_1(in_1[7:4]), .in_2(in_2[7:4]), .Cin(n4bitadder_1_out_8), .out_4(out_4), .out_5(out_5),
    .out_6(out_6), .out_7(out_7), .out_8(Cout));

  // Notes on the sheet:
  //   4 bit adder
  //   4 bit adder
endmodule

module _16bitAdder (
  input  [15:0] in_1,
  input  [15:0] in_2,
  input  Cin,
  output [15:0] out_4,
  output Cout
);

  wire n8bitadder_1_cout;

  _8bitAdder u_8bitadder_1 (
    .in_1(in_1[7:0]), .in_2(in_2[7:0]), .Cin(Cin), .out_4(out_4[7]), .out_5(out_4[6]), .out_6(out_4[5]),
    .out_7(out_4[4]), .out_8(out_4[3]), .out_9(out_4[2]), .out_10(out_4[1]), .out_11(out_4[0]),
    .Cout(n8bitadder_1_cout));
  _8bitAdder u_8bitadder_2 (
    .in_1(in_1[15:8]), .in_2(in_2[15:8]), .Cin(n8bitadder_1_cout), .out_4(out_4[15]), .out_5(out_4[14]),
    .out_6(out_4[13]), .out_7(out_4[12]), .out_8(out_4[11]), .out_9(out_4[10]), .out_10(out_4[9]),
    .out_11(out_4[8]), .Cout(Cout));

  // Notes on the sheet:
  //   8 bit adder
  //   8 bit adder
endmodule

module _20bitAdder (
  input  [19:0] in_1,
  input  [19:0] in_2,
  input  Cin,
  output [19:0] out_4,
  output Cout
);

  wire n16bitadder_1_cout;

  _16bitAdder u_16bitadder_1 (
    .in_1(in_1[15:0]), .in_2(in_2[15:0]), .Cin(Cin), .out_4(out_4[15:0]), .Cout(n16bitadder_1_cout));
  _4bitAdder u_4bitadder_1 (
    .in_1(in_1[19:16]), .in_2(in_2[19:16]), .Cin(n16bitadder_1_cout), .out_4(out_4[19]), .out_5(out_4[18]),
    .out_6(out_4[17]), .out_7(out_4[16]), .out_8(Cout));

  // Notes on the sheet:
  //   16 bit adder
  //   4 bit adder
endmodule

module halfComparator (
  input  a,
  input  b,
  output greater,
  output equal,
  output less_than
);

  wire not_1_out, not_2_out;

  not not_1 (not_1_out, b);
  and and_1 (greater, a, not_1_out);
  xnor xnor_1 (equal, a, b);
  not not_2 (not_2_out, a);
  and and_2 (less_than, not_2_out, b);
endmodule

module fullComparator (
  input  a,
  input  b,
  input  greaterIn,
  input  equalIn,
  input  lessthanIn,
  output greaterOut,
  output lessThanOut,
  output equalOut
);

  wire and_1_out, and_2_out, not_1_out, not_2_out, xnor_1_out;

  not not_1 (not_1_out, a);
  not not_2 (not_2_out, b);
  and and_1 (and_1_out, a, not_2_out, equalIn);
  and and_2 (and_2_out, not_1_out, b, equalIn);
  xnor xnor_1 (xnor_1_out, a, b);
  or or_1 (lessThanOut, and_2_out, lessthanIn);
  and and_3 (equalOut, xnor_1_out, equalIn);
  or or_2 (greaterOut, and_1_out, greaterIn);
endmodule

module _4bitComparator (
  input  [3:0] in_1,
  input  [3:0] in_2,
  output greater,
  output lessThanOut,
  output equalOut
);

  wire fullcomparator_1_equalout, fullcomparator_1_greaterout, fullcomparator_1_lessthanout,
       fullcomparator_2_equalout, fullcomparator_2_greaterout, fullcomparator_2_lessthanout,
       halfcomparator_1_equal, halfcomparator_1_greater, halfcomparator_1_less_than;

  halfComparator halfcomparator_1 (
    .a(in_1[3]), .b(in_2[3]), .greater(halfcomparator_1_greater), .equal(halfcomparator_1_equal),
    .less_than(halfcomparator_1_less_than));
  fullComparator fullcomparator_1 (
    .a(in_1[2]), .b(in_2[2]), .greaterIn(halfcomparator_1_greater), .equalIn(halfcomparator_1_equal),
    .lessthanIn(halfcomparator_1_less_than), .greaterOut(fullcomparator_1_greaterout),
    .lessThanOut(fullcomparator_1_lessthanout), .equalOut(fullcomparator_1_equalout));
  fullComparator fullcomparator_2 (
    .a(in_1[1]), .b(in_2[1]), .greaterIn(fullcomparator_1_greaterout), .equalIn(fullcomparator_1_equalout),
    .lessthanIn(fullcomparator_1_lessthanout), .greaterOut(fullcomparator_2_greaterout),
    .lessThanOut(fullcomparator_2_lessthanout), .equalOut(fullcomparator_2_equalout));
  fullComparator fullcomparator_3 (
    .a(in_1[0]), .b(in_2[0]), .greaterIn(fullcomparator_2_greaterout),
    .equalIn(fullcomparator_2_lessthanout), .lessthanIn(fullcomparator_2_equalout), .greaterOut(greater),
    .lessThanOut(lessThanOut), .equalOut(equalOut));
endmodule

module _20BitComparator (
  input  [19:0] in_1,
  input  [19:0] in_2,
  output greaterOut,
  output lessThanOut,
  output equalOut
);

  wire fullcomparator_1_equalout, fullcomparator_1_greaterout, fullcomparator_1_lessthanout,
       fullcomparator_2_equalout, fullcomparator_2_greaterout, fullcomparator_2_lessthanout,
       fullcomparator_3_equalout, fullcomparator_3_greaterout, fullcomparator_3_lessthanout,
       fullcomparator_4_equalout, fullcomparator_4_greaterout, fullcomparator_4_lessthanout,
       fullcomparator_5_equalout, fullcomparator_5_greaterout, fullcomparator_5_lessthanout,
       fullcomparator_6_equalout, fullcomparator_6_greaterout, fullcomparator_6_lessthanout,
       fullcomparator_7_equalout, fullcomparator_7_greaterout, fullcomparator_7_lessthanout,
       fullcomparator_8_equalout, fullcomparator_8_greaterout, fullcomparator_8_lessthanout,
       fullcomparator_9_equalout, fullcomparator_9_greaterout, fullcomparator_9_lessthanout,
       fullcomparator_10_equalout, fullcomparator_10_greaterout, fullcomparator_10_lessthanout,
       fullcomparator_11_equalout, fullcomparator_11_greaterout, fullcomparator_11_lessthanout,
       fullcomparator_12_equalout, fullcomparator_12_greaterout, fullcomparator_12_lessthanout,
       fullcomparator_13_equalout, fullcomparator_13_greaterout, fullcomparator_13_lessthanout,
       fullcomparator_14_equalout, fullcomparator_14_greaterout, fullcomparator_14_lessthanout,
       fullcomparator_15_equalout, fullcomparator_15_greaterout, fullcomparator_15_lessthanout,
       fullcomparator_16_equalout, fullcomparator_16_greaterout, fullcomparator_16_lessthanout,
       fullcomparator_17_equalout, fullcomparator_17_greaterout, fullcomparator_17_lessthanout,
       fullcomparator_18_equalout, fullcomparator_18_greaterout, fullcomparator_18_lessthanout,
       halfcomparator_1_equal, halfcomparator_1_greater, halfcomparator_1_less_than;

  halfComparator halfcomparator_1 (
    .a(in_1[19]), .b(in_2[19]), .greater(halfcomparator_1_greater), .equal(halfcomparator_1_equal),
    .less_than(halfcomparator_1_less_than));
  fullComparator fullcomparator_1 (
    .a(in_1[14]), .b(in_2[14]), .greaterIn(fullcomparator_16_greaterout),
    .equalIn(fullcomparator_16_equalout), .lessthanIn(fullcomparator_16_lessthanout),
    .greaterOut(fullcomparator_1_greaterout), .lessThanOut(fullcomparator_1_lessthanout),
    .equalOut(fullcomparator_1_equalout));
  fullComparator fullcomparator_2 (
    .a(in_1[9]), .b(in_2[9]), .greaterIn(fullcomparator_17_greaterout), .equalIn(fullcomparator_17_equalout),
    .lessthanIn(fullcomparator_17_lessthanout), .greaterOut(fullcomparator_2_greaterout),
    .lessThanOut(fullcomparator_2_lessthanout), .equalOut(fullcomparator_2_equalout));
  fullComparator fullcomparator_3 (
    .a(in_1[4]), .b(in_2[4]), .greaterIn(fullcomparator_18_greaterout), .equalIn(fullcomparator_18_equalout),
    .lessthanIn(fullcomparator_18_lessthanout), .greaterOut(fullcomparator_3_greaterout),
    .lessThanOut(fullcomparator_3_lessthanout), .equalOut(fullcomparator_3_equalout));
  fullComparator fullcomparator_4 (
    .a(in_1[18]), .b(in_2[18]), .greaterIn(halfcomparator_1_greater), .equalIn(halfcomparator_1_equal),
    .lessthanIn(halfcomparator_1_less_than), .greaterOut(fullcomparator_4_greaterout),
    .lessThanOut(fullcomparator_4_lessthanout), .equalOut(fullcomparator_4_equalout));
  fullComparator fullcomparator_5 (
    .a(in_1[13]), .b(in_2[13]), .greaterIn(fullcomparator_1_greaterout), .equalIn(fullcomparator_1_equalout),
    .lessthanIn(fullcomparator_1_lessthanout), .greaterOut(fullcomparator_5_greaterout),
    .lessThanOut(fullcomparator_5_lessthanout), .equalOut(fullcomparator_5_equalout));
  fullComparator fullcomparator_6 (
    .a(in_1[8]), .b(in_2[8]), .greaterIn(fullcomparator_2_greaterout), .equalIn(fullcomparator_2_equalout),
    .lessthanIn(fullcomparator_2_lessthanout), .greaterOut(fullcomparator_6_greaterout),
    .lessThanOut(fullcomparator_6_lessthanout), .equalOut(fullcomparator_6_equalout));
  fullComparator fullcomparator_7 (
    .a(in_1[3]), .b(in_2[3]), .greaterIn(fullcomparator_3_greaterout), .equalIn(fullcomparator_3_equalout),
    .lessthanIn(fullcomparator_3_lessthanout), .greaterOut(fullcomparator_7_greaterout),
    .lessThanOut(fullcomparator_7_lessthanout), .equalOut(fullcomparator_7_equalout));
  fullComparator fullcomparator_8 (
    .a(in_1[17]), .b(in_2[17]), .greaterIn(fullcomparator_4_greaterout), .equalIn(fullcomparator_4_equalout),
    .lessthanIn(fullcomparator_4_lessthanout), .greaterOut(fullcomparator_8_greaterout),
    .lessThanOut(fullcomparator_8_lessthanout), .equalOut(fullcomparator_8_equalout));
  fullComparator fullcomparator_9 (
    .a(in_1[12]), .b(in_2[12]), .greaterIn(fullcomparator_5_greaterout), .equalIn(fullcomparator_5_equalout),
    .lessthanIn(fullcomparator_5_lessthanout), .greaterOut(fullcomparator_9_greaterout),
    .lessThanOut(fullcomparator_9_lessthanout), .equalOut(fullcomparator_9_equalout));
  fullComparator fullcomparator_10 (
    .a(in_1[7]), .b(in_2[7]), .greaterIn(fullcomparator_6_greaterout), .equalIn(fullcomparator_6_equalout),
    .lessthanIn(fullcomparator_6_lessthanout), .greaterOut(fullcomparator_10_greaterout),
    .lessThanOut(fullcomparator_10_lessthanout), .equalOut(fullcomparator_10_equalout));
  fullComparator fullcomparator_11 (
    .a(in_1[2]), .b(in_2[2]), .greaterIn(fullcomparator_7_greaterout), .equalIn(fullcomparator_7_equalout),
    .lessthanIn(fullcomparator_7_lessthanout), .greaterOut(fullcomparator_11_greaterout),
    .lessThanOut(fullcomparator_11_lessthanout), .equalOut(fullcomparator_11_equalout));
  fullComparator fullcomparator_12 (
    .a(in_1[16]), .b(in_2[16]), .greaterIn(fullcomparator_8_greaterout), .equalIn(fullcomparator_8_equalout),
    .lessthanIn(fullcomparator_8_lessthanout), .greaterOut(fullcomparator_12_greaterout),
    .lessThanOut(fullcomparator_12_lessthanout), .equalOut(fullcomparator_12_equalout));
  fullComparator fullcomparator_13 (
    .a(in_1[11]), .b(in_2[11]), .greaterIn(fullcomparator_9_greaterout), .equalIn(fullcomparator_9_equalout),
    .lessthanIn(fullcomparator_9_lessthanout), .greaterOut(fullcomparator_13_greaterout),
    .lessThanOut(fullcomparator_13_lessthanout), .equalOut(fullcomparator_13_equalout));
  fullComparator fullcomparator_14 (
    .a(in_1[6]), .b(in_2[6]), .greaterIn(fullcomparator_10_greaterout), .equalIn(fullcomparator_10_equalout),
    .lessthanIn(fullcomparator_10_lessthanout), .greaterOut(fullcomparator_14_greaterout),
    .lessThanOut(fullcomparator_14_lessthanout), .equalOut(fullcomparator_14_equalout));
  fullComparator fullcomparator_15 (
    .a(in_1[1]), .b(in_2[1]), .greaterIn(fullcomparator_11_greaterout), .equalIn(fullcomparator_11_equalout),
    .lessthanIn(fullcomparator_11_lessthanout), .greaterOut(fullcomparator_15_greaterout),
    .lessThanOut(fullcomparator_15_lessthanout), .equalOut(fullcomparator_15_equalout));
  fullComparator fullcomparator_16 (
    .a(in_1[15]), .b(in_2[15]), .greaterIn(fullcomparator_12_greaterout),
    .equalIn(fullcomparator_12_equalout), .lessthanIn(fullcomparator_12_lessthanout),
    .greaterOut(fullcomparator_16_greaterout), .lessThanOut(fullcomparator_16_lessthanout),
    .equalOut(fullcomparator_16_equalout));
  fullComparator fullcomparator_17 (
    .a(in_1[10]), .b(in_2[10]), .greaterIn(fullcomparator_13_greaterout),
    .equalIn(fullcomparator_13_equalout), .lessthanIn(fullcomparator_13_lessthanout),
    .greaterOut(fullcomparator_17_greaterout), .lessThanOut(fullcomparator_17_lessthanout),
    .equalOut(fullcomparator_17_equalout));
  fullComparator fullcomparator_18 (
    .a(in_1[5]), .b(in_2[5]), .greaterIn(fullcomparator_14_greaterout), .equalIn(fullcomparator_14_equalout),
    .lessthanIn(fullcomparator_14_lessthanout), .greaterOut(fullcomparator_18_greaterout),
    .lessThanOut(fullcomparator_18_lessthanout), .equalOut(fullcomparator_18_equalout));
  fullComparator fullcomparator_19 (
    .a(in_1[0]), .b(in_2[0]), .greaterIn(fullcomparator_15_greaterout), .equalIn(fullcomparator_15_equalout),
    .lessthanIn(fullcomparator_15_lessthanout), .greaterOut(greaterOut), .lessThanOut(lessThanOut),
    .equalOut(equalOut));

  // Notes on the sheet:
  //   half comparator
  //   full comparator
endmodule

module fullSubtractor (
  input  a,
  input  b,
  input  borrowIN,
  output Difference,
  output BorrowOut
);

  wire and_1_out, and_2_out, not_1_out, not_2_out, xor_1_out;

  not not_1 (not_1_out, a);
  xor xor_1 (xor_1_out, a, b);
  and and_1 (and_1_out, not_1_out, b);
  and and_2 (and_2_out, borrowIN, not_2_out);
  not not_2 (not_2_out, xor_1_out);
  or or_1 (BorrowOut, and_2_out, and_1_out);
  xor xor_2 (Difference, xor_1_out, borrowIN);
endmodule

module _4bitSubtractor (
  input  [3:0] in_1,
  input  [3:0] in_2,
  input  borrowIN,
  output [3:0] out_4,
  output borrowOut
);

  wire fullsubtractor_1_borrowout, fullsubtractor_2_borrowout, fullsubtractor_3_borrowout;

  fullSubtractor fullsubtractor_1 (
    .a(in_1[0]), .b(in_2[0]), .borrowIN(borrowIN), .Difference(out_4[0]),
    .BorrowOut(fullsubtractor_1_borrowout));
  fullSubtractor fullsubtractor_2 (
    .a(in_1[1]), .b(in_2[1]), .borrowIN(fullsubtractor_1_borrowout), .Difference(out_4[1]),
    .BorrowOut(fullsubtractor_2_borrowout));
  fullSubtractor fullsubtractor_3 (
    .a(in_1[2]), .b(in_2[2]), .borrowIN(fullsubtractor_2_borrowout), .Difference(out_4[2]),
    .BorrowOut(fullsubtractor_3_borrowout));
  fullSubtractor fullsubtractor_4 (
    .a(in_1[3]), .b(in_2[3]), .borrowIN(fullsubtractor_3_borrowout), .Difference(out_4[3]),
    .BorrowOut(borrowOut));
endmodule

module _8bitSubtractor (
  input  [7:0] in_1,
  input  [7:0] in_2,
  input  BorrowIn,
  output [7:0] out_4,
  output BorrowOut
);

  wire n4bitsubtractor_1_borrowout;

  _4bitSubtractor u_4bitsubtractor_1 (
    .in_1(in_1[3:0]), .in_2(in_2[3:0]), .borrowIN(BorrowIn), .out_4(out_4[3:0]),
    .borrowOut(n4bitsubtractor_1_borrowout));
  _4bitSubtractor u_4bitsubtractor_2 (
    .in_1(in_1[7:4]), .in_2(in_2[7:4]), .borrowIN(n4bitsubtractor_1_borrowout), .out_4(out_4[7:4]),
    .borrowOut(BorrowOut));
endmodule

module _16bitSubtractor (
  input  [15:0] in_1,
  input  [15:0] in_2,
  input  BorrowIn,
  output [15:0] out_4,
  output BorrowOut
);

  wire n8bitsubtractor_1_borrowout;

  _8bitSubtractor u_8bitsubtractor_1 (
    .in_1(in_1[7:0]), .in_2(in_2[7:0]), .BorrowIn(BorrowIn), .out_4(out_4[7:0]),
    .BorrowOut(n8bitsubtractor_1_borrowout));
  _8bitSubtractor u_8bitsubtractor_2 (
    .in_1(in_1[15:8]), .in_2(in_2[15:8]), .BorrowIn(n8bitsubtractor_1_borrowout), .out_4(out_4[15:8]),
    .BorrowOut(BorrowOut));
endmodule

module _20bitSubtractor (
  input  [19:0] in_1,
  input  [19:0] in_2,
  input  BorrowIn,
  output [19:0] out_4,
  output borrowOut
);

  wire _16bitSubtractor_borrowout;

  _16bitSubtractor _16bitSubtractor (
    .in_1(in_1[15:0]), .in_2(in_2[15:0]), .BorrowIn(BorrowIn), .out_4(out_4[15:0]),
    .BorrowOut(_16bitSubtractor_borrowout));
  _4bitSubtractor _4bitSubtractor (
    .in_1(in_1[19:16]), .in_2(in_2[19:16]), .borrowIN(_16bitSubtractor_borrowout), .out_4(out_4[19:16]),
    .borrowOut(borrowOut));
endmodule

module dFlipFlop (
  input  D,
  input  CLK,
  output Q,
  output Q_prime
);

  wire nand_1_out, nand_2_out, not_1_out;

  not not_1 (not_1_out, D);
  nand nand_1 (nand_1_out, D, CLK);
  nand nand_2 (nand_2_out, not_1_out, CLK);
  nand nand_3 (Q, nand_1_out, Q_prime);
  nand nand_4 (Q_prime, Q, nand_2_out);
endmodule

module _2bitRegister (
  input  [1:0] in_1,
  input  in_2,
  output [1:0] out_3
);

  dFlipFlop dflipflop_1 (.D(in_1[0]), .CLK(in_2), .Q(out_3[0]));  // open: Q_prime
  dFlipFlop dflipflop_2 (.D(in_1[1]), .CLK(in_2), .Q(out_3[1]));  // open: Q_prime
endmodule

module _4bitRegister (
  input  [3:0] in_1,
  input  in_2,
  output [3:0] out_3
);

  _2bitRegister u_2bitregister_1 (.in_1(in_1[1:0]), .in_2(in_2), .out_3(out_3[1:0]));
  _2bitRegister u_2bitregister_2 (.in_1(in_1[3:2]), .in_2(in_2), .out_3(out_3[3:2]));
endmodule

module _8bitRegister (
  input  [7:0] in_1,
  input  in_2,
  output [7:0] out_3
);

  _4bitRegister u_4bitregister_1 (.in_1(in_1[3:0]), .in_2(in_2), .out_3(out_3[3:0]));
  _4bitRegister u_4bitregister_2 (.in_1(in_1[7:4]), .in_2(in_2), .out_3(out_3[7:4]));
endmodule

module _16bitRegister (
  input  [15:0] in_1,
  input  in_2,
  output [15:0] out_3
);

  _8bitRegister u_8bitregister_1 (.in_1(in_1[7:0]), .in_2(in_2), .out_3(out_3[7:0]));
  _8bitRegister u_8bitregister_2 (.in_1(in_1[15:8]), .in_2(in_2), .out_3(out_3[15:8]));
endmodule

module _20bitRegister (
  input  [19:0] in_1,
  input  in_2,
  output [19:0] out_3
);

  _4bitRegister u_4bitregister_1 (.in_1(in_1[3:0]), .in_2(in_2), .out_3(out_3[3:0]));
  _4bitRegister u_4bitregister_2 (.in_1(in_1[7:4]), .in_2(in_2), .out_3(out_3[7:4]));
  _4bitRegister u_4bitregister_3 (.in_1(in_1[11:8]), .in_2(in_2), .out_3(out_3[11:8]));
  _4bitRegister u_4bitregister_4 (.in_1(in_1[15:12]), .in_2(in_2), .out_3(out_3[15:12]));
  _4bitRegister u_4bitregister_5 (.in_1(in_1[19:16]), .in_2(in_2), .out_3(out_3[19:16]));
endmodule

module testregister (
  input  [19:0] in_1,
  output [19:0] out_2
);

  wire clock_1_out;

  Clock clock_1 (.out(clock_1_out));
endmodule

// pc
module programCounter (
  input  [19:0] \input ,
  input  in_2,
  input  enable,
  input  clock,
  output [19:0] \output 
);

  wire [19:0] adder_1_out, multiplexer_1_out;

  Multiplexer #(.width(20), .enable("false")) multiplexer_1 (
    .in0(adder_1_out), .in1(\input ), .out(multiplexer_1_out), .sel(in_2));
  Adder #(.width(20)) adder_1 (.a(\output ), .b(20'h1), .out(adder_1_out));  // open: cin, cout
  Register #(.width(20)) register_1 (.D(multiplexer_1_out), .en(enable), .Q(\output ), .clk(clock), .clr(1'b0));
endmodule

// ext7
module extender7to20 (
  input  [6:0] in_1,
  output [19:0] out_2
);


  assign out_2 = {{14{in_1[6]}}, in_1[5:0]};
endmodule

// ext11
module extender11to20 (
  input  [10:0] input_11_bit,
  output [19:0] output_20_bit
);


  assign output_20_bit = {{10{input_11_bit[10]}}, input_11_bit[9:0]};
endmodule

// reducer
module extender15to20 (
  input  [14:0] \input ,
  output [19:0] \output 
);


  assign \output  = {{6{\input [14]}}, \input [13:0]};
endmodule

module alu (
  input  [19:0] input1,
  input  [19:0] input2,
  input  in,
  input  [3:0] alu_control,
  output [19:0] \output 
);

  wire [19:0] and_1_out, n20bitadder_1_out_4, n20bitsubtractor_1_out_4, or_1_out, xor_1_out;

  _20bitAdder u_20bitadder_1 (.in_1(input1), .in_2(input2), .Cin(in), .out_4(n20bitadder_1_out_4));  // open: Cout
  _20bitSubtractor u_20bitsubtractor_1 (
    .in_1(input1), .in_2(input2), .BorrowIn(in), .out_4(n20bitsubtractor_1_out_4));  // open: borrowOut
  assign and_1_out = input1 & input2;  // AND_Gate and_1, 20 bits wide
  assign or_1_out = input1 | input2;  // OR_Gate or_1, 20 bits wide
  assign xor_1_out = input1 ^ input2;  // XOR_Gate xor_1, 20 bits wide
  Multiplexer #(.select(4), .width(20), .enable("false")) multiplexer_1 (
    .in0(n20bitadder_1_out_4), .in1(n20bitsubtractor_1_out_4), .in2(and_1_out), .in3(or_1_out),
    .in4(xor_1_out), .out(\output ), .sel(alu_control));  // open: in5, in6, in7, in8, in9, in10, in11, in12, in13, in14, in15
endmodule

// regFile
module registerFile (
  input  [3:0] write_register,
  input  [3:0] read_register_data_1,
  input  [3:0] read_register_data_2,
  input  [19:0] write_data,
  input  reg_write,
  input  clock,
  output [19:0] output1,
  output [19:0] output2
);

  wire and_1_out, and_2_out, and_3_out, and_4_out, and_5_out, and_6_out, and_7_out, and_8_out, and_9_out,
       and_10_out, and_11_out, and_12_out, and_13_out, and_14_out, and_15_out, and_16_out, decoder_1_out0,
       decoder_1_out1, decoder_1_out2, decoder_1_out3, decoder_1_out4, decoder_1_out5, decoder_1_out6,
       decoder_1_out7, decoder_1_out8, decoder_1_out9, decoder_1_out10, decoder_1_out11, decoder_1_out12,
       decoder_1_out13, decoder_1_out14, decoder_1_out15;
  wire [19:0] register_1_q, register_2_q, register_3_q, register_4_q, register_5_q, register_6_q,
       register_7_q, register_8_q, register_9_q, register_10_q, register_11_q, register_12_q, register_13_q,
       register_14_q, register_15_q, register_16_q;

  Decoder #(.select(4), .enable("false")) decoder_1 (
    .out0(decoder_1_out0), .out1(decoder_1_out1), .out2(decoder_1_out2), .out3(decoder_1_out3),
    .out4(decoder_1_out4), .out5(decoder_1_out5), .out6(decoder_1_out6), .out7(decoder_1_out7),
    .out8(decoder_1_out8), .out9(decoder_1_out9), .out10(decoder_1_out10), .out11(decoder_1_out11),
    .out12(decoder_1_out12), .out13(decoder_1_out13), .out14(decoder_1_out14), .out15(decoder_1_out15),
    .sel(write_register));
  and and_1 (and_1_out, decoder_1_out0, reg_write);
  and and_2 (and_2_out, decoder_1_out1, reg_write);
  and and_3 (and_3_out, decoder_1_out2, reg_write);
  and and_4 (and_4_out, decoder_1_out3, reg_write);
  and and_5 (and_5_out, decoder_1_out4, reg_write);
  and and_6 (and_6_out, decoder_1_out5, reg_write);
  and and_7 (and_7_out, decoder_1_out6, reg_write);
  and and_8 (and_8_out, decoder_1_out7, reg_write);
  Register #(.width(20)) register_1 (.D(write_data), .en(and_1_out), .Q(register_1_q), .clk(clock));  // open: clr
  Register #(.width(20)) register_2 (.D(write_data), .en(and_2_out), .Q(register_2_q), .clk(clock));  // open: clr
  Register #(.width(20)) register_3 (.D(write_data), .en(and_3_out), .Q(register_3_q), .clk(clock));  // open: clr
  Register #(.width(20)) register_4 (.D(write_data), .en(and_4_out), .Q(register_4_q), .clk(clock));  // open: clr
  Register #(.width(20)) register_5 (.D(write_data), .en(and_5_out), .Q(register_5_q), .clk(clock));  // open: clr
  Register #(.width(20)) register_6 (.D(write_data), .en(and_6_out), .Q(register_6_q), .clk(clock));  // open: clr
  Register #(.width(20)) register_7 (.D(write_data), .en(and_7_out), .Q(register_7_q), .clk(clock));  // open: clr
  Register #(.width(20)) register_8 (.D(write_data), .en(and_8_out), .Q(register_8_q), .clk(clock));  // open: clr
  and and_9 (and_9_out, decoder_1_out8, reg_write);
  and and_10 (and_10_out, decoder_1_out9, reg_write);
  and and_11 (and_11_out, decoder_1_out10, reg_write);
  and and_12 (and_12_out, decoder_1_out11, reg_write);
  and and_13 (and_13_out, decoder_1_out12, reg_write);
  and and_14 (and_14_out, decoder_1_out13, reg_write);
  and and_15 (and_15_out, decoder_1_out14, reg_write);
  and and_16 (and_16_out, decoder_1_out15, reg_write);
  Register #(.width(20)) register_9 (.D(write_data), .en(and_9_out), .Q(register_9_q), .clk(clock));  // open: clr
  Register #(.width(20)) register_10 (.D(write_data), .en(and_10_out), .Q(register_10_q), .clk(clock));  // open: clr
  Register #(.width(20)) register_11 (.D(write_data), .en(and_11_out), .Q(register_11_q), .clk(clock));  // open: clr
  Register #(.width(20)) register_12 (.D(write_data), .en(and_12_out), .Q(register_12_q), .clk(clock));  // open: clr
  Register #(.width(20)) register_13 (.D(write_data), .en(and_13_out), .Q(register_13_q), .clk(clock));  // open: clr
  Register #(.width(20)) register_14 (.D(write_data), .en(and_14_out), .Q(register_14_q), .clk(clock));  // open: clr
  Register #(.width(20)) register_15 (.D(write_data), .en(and_15_out), .Q(register_15_q), .clk(clock));  // open: clr
  Register #(.width(20)) register_16 (.D(write_data), .en(and_16_out), .Q(register_16_q), .clk(clock));  // open: clr
  Multiplexer #(.select(4), .width(20), .enable("false")) multiplexer_1 (
    .in0(register_1_q), .in1(register_2_q), .in2(register_3_q), .in3(register_4_q), .in4(register_5_q),
    .in5(register_6_q), .in6(register_7_q), .in7(register_8_q), .in8(register_9_q), .in9(register_10_q),
    .in10(register_11_q), .in11(register_12_q), .in12(register_13_q), .in13(register_14_q),
    .in14(register_15_q), .in15(register_16_q), .out(output1), .sel(read_register_data_1));
  Multiplexer #(.select(4), .width(20), .enable("false")) multiplexer_2 (
    .in0(register_1_q), .in1(register_2_q), .in2(register_3_q), .in3(register_4_q), .in4(register_5_q),
    .in5(register_6_q), .in6(register_7_q), .in7(register_8_q), .in8(register_9_q), .in9(register_10_q),
    .in10(register_11_q), .in11(register_12_q), .in12(register_13_q), .in13(register_14_q),
    .in14(register_15_q), .in15(register_16_q), .out(output2), .sel(read_register_data_2));
endmodule

// cu
module controlUnit (
  input  [19:0] \input ,
  input  clock,
  output [3:0] alu_control,
  output immediate_code,
  output [3:0] writeReg,
  output regWrite,
  output [19:0] alu_in1,
  output pc_enable,
  output [19:0] pc_in,
  output [19:0] alu_in2,
  output [3:0] reg_1,
  output [3:0] reg_2
);

  wire decoder_1_out0, decoder_1_out1, decoder_1_out2, decoder_1_out3, decoder_1_out4, decoder_1_out5,
       decoder_1_out6, decoder_1_out7, decoder_1_out8, decoder_1_out9, decoder_1_out10, decoder_1_out11,
       decoder_1_out12, or_2_out;
  wire [19:0] alu_1_output, extender7to20_1_out_2, extender11to20_1_output_20_bit, extender15to20_1_output,
       multiplexer_1_out, multiplexer_2_out, registerfile_1_output1;

  extender15to20 extender15to20_1 (
    .\input ({\input [8:5], \input [12:9], \input [15:13], \input [19:16]}),
    .\output (extender15to20_1_output));
  extender11to20 extender11to20_1 (
    .input_11_bit({\input [12:9], \input [15:13], \input [19:16]}),
    .output_20_bit(extender11to20_1_output_20_bit));
  Multiplexer #(.width(20), .enable("false")) multiplexer_1 (
    .in0(extender11to20_1_output_20_bit), .in1(extender15to20_1_output), .out(multiplexer_1_out),
    .sel(pc_enable));
  Multiplexer #(.width(20), .enable("false")) multiplexer_2 (
    .in0(alu_1_output), .in1(extender11to20_1_output_20_bit), .out(multiplexer_2_out), .sel(decoder_1_out10));
  programCounter programcounter_1 (
    .\input (multiplexer_1_out), .clock(clock), .in_2(decoder_1_out11), .enable(pc_enable), .\output (pc_in));
  extender7to20 extender7to20_1 (.in_1(\input [19:13]), .out_2(extender7to20_1_out_2));
  registerFile registerfile_1 (
    .read_register_data_1(\input [19:16]), .read_register_data_2(\input [12:9]),
    .write_data(multiplexer_2_out), .clock(clock), .write_register(\input [8:5]), .reg_write(or_2_out),
    .output1(registerfile_1_output1), .output2(alu_in2));
  registerFile registerfile_2 (
    .write_data(pc_in), .write_register(\input [8:5]), .reg_write(decoder_1_out11));  // open: read_register_data_1, read_register_data_2, clock, output1, output2
  or or_1 (pc_enable, decoder_1_out11, decoder_1_out12);
  Multiplexer #(.width(20), .enable("false")) multiplexer_3 (
    .in0(registerfile_1_output1), .in1(extender7to20_1_out_2), .out(alu_in1), .sel(\input [4]));
  alu alu_1 (.input1(alu_in1), .input2(alu_in2), .alu_control(\input [3:0]), .\output (alu_1_output));  // open: in
  Decoder #(.select(4), .enable("false")) decoder_1 (
    .out0(decoder_1_out0), .out1(decoder_1_out1), .out2(decoder_1_out2), .out3(decoder_1_out3),
    .out4(decoder_1_out4), .out5(decoder_1_out5), .out6(decoder_1_out6), .out7(decoder_1_out7),
    .out8(decoder_1_out8), .out9(decoder_1_out9), .out10(decoder_1_out10), .out11(decoder_1_out11),
    .out12(decoder_1_out12), .sel(\input [3:0]));  // open: out13, out14, out15
  or or_2 (or_2_out, decoder_1_out0, decoder_1_out1, decoder_1_out2, decoder_1_out3, decoder_1_out4, decoder_1_out5, decoder_1_out6, decoder_1_out7, decoder_1_out8, decoder_1_out9);
  or or_3 (regWrite, or_2_out, decoder_1_out11, decoder_1_out12);

  assign alu_control = \input [3:0];
  assign immediate_code = \input [4];
  assign reg_1 = \input [12:9];
  assign reg_2 = \input [19:16];
  assign writeReg = \input [8:5];

  // Notes on the sheet:
  //   load
endmodule

module cpu (
  input  cin,
  input  in_2,
  output immediate_code
);

  wire clock_1_out, controlunit_1_pc_enable, controlunit_1_regwrite;
  wire [3:0] controlunit_1_alu_control, controlunit_1_reg_1, controlunit_1_reg_2, controlunit_1_writereg;
  wire [19:0] alu_1_output, controlunit_1_alu_in1, controlunit_1_alu_in2, controlunit_1_pc_in,
       multiplexer_1_out, programcounter_1_output, registerfile_1_output1, registerfile_1_output2, rom_1_data;

  Clock clock_1 (.out(clock_1_out));
  programCounter programcounter_1 (
    .\input (controlunit_1_pc_in), .clock(clock_1_out), .enable(controlunit_1_pc_enable),
    .\output (programcounter_1_output));  // open: in_2
  ROM #(.addrWidth(20), .dataWidth(20)) rom_1 (.addr(programcounter_1_output), .data(rom_1_data));  // open: sel
  controlUnit controlunit_1 (
    .\input (rom_1_data), .clock(clock_1_out), .pc_enable(controlunit_1_pc_enable),
    .alu_control(controlunit_1_alu_control), .immediate_code(immediate_code),
    .alu_in1(controlunit_1_alu_in1), .pc_in(controlunit_1_pc_in), .alu_in2(controlunit_1_alu_in2),
    .reg_2(controlunit_1_reg_2), .reg_1(controlunit_1_reg_1), .regWrite(controlunit_1_regwrite),
    .writeReg(controlunit_1_writereg));
  registerFile registerfile_1 (
    .read_register_data_1(controlunit_1_reg_1), .read_register_data_2(controlunit_1_reg_2),
    .write_data(alu_1_output), .clock(clock_1_out), .write_register(controlunit_1_writereg),
    .reg_write(controlunit_1_regwrite), .output1(registerfile_1_output1), .output2(registerfile_1_output2));
  alu alu_1 (
    .input1(controlunit_1_alu_in1), .input2(controlunit_1_alu_in2), .in(cin),
    .alu_control(controlunit_1_alu_control), .\output (alu_1_output));
  Multiplexer #(.width(20), .enable("false")) multiplexer_1 (
    .in0(registerfile_1_output1), .in1(registerfile_1_output2), .out(multiplexer_1_out), .sel(in_2));
  RAM #(.addrWidth(20), .dataWidth(20), .bus("separate")) ram_1 (.addr(multiplexer_1_out));  // open: din, data, str, sel, clk, ld, clr

  // Notes on the sheet:
  //   contents of rom_1 (hex, n*v repeats v):
  //   988d 6280c 7000c 2802
endmodule
